// Logisim project pcu6.circ as structural Verilog: 1 circuit, main circuit main
module main (
);

  wire adder_1_cout, and_1_out, and_2_out, and_4_out, and_5_out, and_6_out, and_7_out, and_8_out, and_9_out,
       and_10_out, and_11_out, and_12_out, and_13_out, and_14_out, and_15_out, and_16_out, button_1_out,
       button_2_out, clock_1_out, d_ff_1_q, d_ff_2_q, d_ff_4_q, demultiplexer_1_out0, demultiplexer_1_out1,
       demultiplexer_1_out2, demultiplexer_1_out3, demultiplexer_2_out0, demultiplexer_2_out1,
       demultiplexer_2_out2, demultiplexer_2_out3, demultiplexer_2_out4, demultiplexer_2_out5,
       demultiplexer_2_out6, demultiplexer_2_out7, demultiplexer_2_out10, demultiplexer_2_out11,
       demultiplexer_2_out12, demultiplexer_2_out13, demultiplexer_3_out0, demultiplexer_3_out1,
       demultiplexer_3_out2, demultiplexer_3_out3, demultiplexer_3_out4, demultiplexer_3_out5,
       demultiplexer_3_out6, demultiplexer_3_out7, demultiplexer_4_out0, demultiplexer_4_out12,
       demultiplexer_4_out13, demultiplexer_4_out14, demultiplexer_4_out15, demultiplexer_5_out0,
       demultiplexer_5_out1, nor_2_out, nor_3_out, not_1_out, or_1_out, or_2_out, or_3_out, or_4_out,
       or_5_out, or_6_out, or_7_out, or_9_out, or_10_out, or_11_out, or_12_out, or_13_out, or_14_out,
       or_15_out, s_r_ff_1_qn, xor_1_out, xor_2_out, xor_3_out;
  wire [0:0] counter_1_q;
  wire [1:1] counter_1_q_2;
  wire [3:0] controlled_buffer_5_out_2;
  wire [6:0] bit_extender_1_out;
  wire [6:6] register_5_q;
  wire [7:0] adder_1_out, and_3_out, controlled_buffer_3_out, controlled_buffer_6_out, counter_2_q,
       counter_3_q, d_ff_3_q, nor_1_out, or_8_out, ram_1_dout, register_1_q, register_2_q, register_3_q,
       register_4_q, rgb_video_1_p4, rgb_video_1_p5, rom_1_data;
  wire [7:4] controlled_buffer_5_out;
  wire [9:0] controlled_buffer_1_out;

  Clock clock_1 (.out(clock_1_out));
  assign controlled_buffer_1_out = or_1_out ? {1'b0, counter_3_q, counter_1_q[0]} : 10'bz;  // Controlled_Buffer controlled_buffer_1
  Counter #(.max('h3), .width(2)) counter_1 (
    .clr(button_2_out), .load(1'b0), .up(1'b1), .count(1'b1), .clk(clock_1_out),
    .Q({counter_1_q_2[1], counter_1_q[0]}));  // open: D, carry
  ROM #(.addrWidth(10)) rom_1 (.addr(controlled_buffer_1_out), .data(rom_1_data));
  assign controlled_buffer_1_out = demultiplexer_1_out2 ? {2'b10, controlled_buffer_5_out, controlled_buffer_5_out_2} : 10'bz;  // Controlled_Buffer controlled_buffer_2
  or or_1 (or_1_out, demultiplexer_1_out1, demultiplexer_1_out0);
  Demultiplexer #(.select(2)) demultiplexer_1 (
    .out0(demultiplexer_1_out0), .out1(demultiplexer_1_out1), .out2(demultiplexer_1_out2),
    .out3(demultiplexer_1_out3), .in(1'b1), .sel({counter_1_q_2[1], counter_1_q[0]}));
  Register register_1 (
    .D(rom_1_data), .en(demultiplexer_1_out0), .clk(clock_1_out), .Q(register_1_q), .clr(button_2_out));
  Register register_2 (
    .D(rom_1_data), .en(demultiplexer_1_out1), .clk(clock_1_out), .Q(register_2_q), .clr(button_2_out));
  Demultiplexer #(.select(4)) demultiplexer_2 (
    .out0(demultiplexer_2_out0), .out1(demultiplexer_2_out1), .out2(demultiplexer_2_out2),
    .out3(demultiplexer_2_out3), .out4(demultiplexer_2_out4), .out5(demultiplexer_2_out5),
    .out6(demultiplexer_2_out6), .out7(demultiplexer_2_out7), .out10(demultiplexer_2_out10),
    .out11(demultiplexer_2_out11), .out12(demultiplexer_2_out12), .out13(demultiplexer_2_out13),
    .in(demultiplexer_1_out2), .sel(register_2_q[3:0]));  // open: out8, out9, out14, out15
  or or_2 (or_2_out, demultiplexer_2_out0, demultiplexer_2_out1, demultiplexer_2_out2, demultiplexer_2_out3, demultiplexer_2_out4, demultiplexer_2_out5);
  or or_3 (or_3_out, or_2_out, demultiplexer_2_out6);
  assign controlled_buffer_3_out = or_5_out ? rom_1_data : 8'bz;  // Controlled_Buffer controlled_buffer_3
  or or_4 (or_4_out, demultiplexer_2_out10, demultiplexer_2_out11);
  Demultiplexer #(.select(3)) demultiplexer_3 (
    .out0(demultiplexer_3_out0), .out1(demultiplexer_3_out1), .out2(demultiplexer_3_out2),
    .out3(demultiplexer_3_out3), .out4(demultiplexer_3_out4), .out5(demultiplexer_3_out5),
    .out6(demultiplexer_3_out6), .out7(demultiplexer_3_out7), .in(or_3_out), .sel(register_2_q[6:4]));
  or or_5 (or_5_out, demultiplexer_2_out12, demultiplexer_2_out13);
  Counter counter_2 (
    .clr(button_2_out), .load(demultiplexer_2_out2), .up(demultiplexer_2_out10), .count(or_4_out),
    .clk(clock_1_out), .D(controlled_buffer_3_out), .Q(counter_2_q));  // open: carry
  assign controlled_buffer_3_out = demultiplexer_3_out0 ? register_1_q : 8'bz;  // Controlled_Buffer controlled_buffer_4
  or or_6 (or_6_out, demultiplexer_2_out0, demultiplexer_2_out12);
  or or_7 (or_7_out, demultiplexer_2_out1, demultiplexer_2_out13);
  Register register_3 (
    .D(controlled_buffer_3_out), .en(or_6_out), .clk(clock_1_out), .Q(register_3_q), .clr(button_2_out));
  Register register_4 (
    .D(controlled_buffer_3_out), .en(or_7_out), .clk(clock_1_out), .Q(register_4_q), .clr(button_2_out));
  assign {controlled_buffer_5_out, controlled_buffer_5_out_2} = register_2_q[7] ? counter_2_q : 8'bz;  // Controlled_Buffer controlled_buffer_5
  assign controlled_buffer_6_out = register_2_q[7] ? register_4_q : 8'bz;  // Controlled_Buffer controlled_buffer_6
  not not_1 (not_1_out, register_2_q[7]);
  assign controlled_buffer_6_out = not_1_out ? register_1_q : 8'bz;  // Controlled_Buffer controlled_buffer_7
  assign {controlled_buffer_5_out, controlled_buffer_5_out_2} = not_1_out ? register_1_q : 8'bz;  // Controlled_Buffer controlled_buffer_8
  RAM #(.asyncread("true")) ram_1 (
    .addr({controlled_buffer_5_out, controlled_buffer_5_out_2}), .we(demultiplexer_2_out3),
    .oe(demultiplexer_3_out7), .clk(and_1_out), .din(controlled_buffer_3_out), .dout(ram_1_dout));
  and and_1 (and_1_out, clock_1_out, ~and_2_out);  // AND_Gate
  and and_2 (and_2_out, controlled_buffer_5_out[4], controlled_buffer_5_out[5], controlled_buffer_5_out[6], controlled_buffer_5_out[7]);
  Demultiplexer #(.enable("true"), .select(4)) demultiplexer_4 (
    .out0(demultiplexer_4_out0), .out12(demultiplexer_4_out12), .out13(demultiplexer_4_out13),
    .out14(demultiplexer_4_out14), .out15(demultiplexer_4_out15), .in(demultiplexer_2_out3),
    .sel(controlled_buffer_5_out_2), .en(and_2_out));  // open: out1, out2, out3, out4, out5, out6, out7, out8, out9, out10, out11
  Demultiplexer #(.enable("true"), .select(4)) demultiplexer_5 (
    .out0(demultiplexer_5_out0), .out1(demultiplexer_5_out1), .in(demultiplexer_3_out7),
    .sel(controlled_buffer_5_out_2), .en(and_2_out));  // open: out2, out3, out4, out5, out6, out7, out8, out9, out10, out11, out12, out13, out14, out15
  S_R_Flip_Flop s_r_ff_1 (
    .S(or_9_out), .R(demultiplexer_1_out0), .clk(clock_1_out), .Qn(s_r_ff_1_qn));  // open: Q, reset, preset
  Adder adder_1 (.a(register_3_q), .b(controlled_buffer_6_out), .out(adder_1_out), .cin(d_ff_1_q), .cout(adder_1_cout));
  assign and_3_out = register_3_q & controlled_buffer_6_out;  // AND_Gate and_3, 8 bits wide
  assign or_8_out = register_3_q | controlled_buffer_6_out;  // OR_Gate or_8, 8 bits wide
  assign nor_1_out = ~(register_3_q | controlled_buffer_6_out);  // NOR_Gate nor_1, 8 bits wide
  and and_4 (and_4_out, demultiplexer_2_out5, d_ff_3_q[0]);
  or or_9 (or_9_out, demultiplexer_2_out4, and_4_out);
  Counter counter_3 (
    .clr(button_2_out), .load(or_9_out), .up(1'b1), .count(and_5_out), .clk(clock_1_out),
    .D(controlled_buffer_3_out), .Q(counter_3_q));  // open: carry
  and and_5 (and_5_out, s_r_ff_1_qn, demultiplexer_1_out3);
  assign controlled_buffer_3_out = demultiplexer_3_out3 ? adder_1_out : 8'bz;  // Controlled_Buffer controlled_buffer_9
  assign controlled_buffer_3_out = demultiplexer_3_out4 ? and_3_out : 8'bz;  // Controlled_Buffer controlled_buffer_10
  assign controlled_buffer_3_out = demultiplexer_3_out5 ? or_8_out : 8'bz;  // Controlled_Buffer controlled_buffer_11
  assign controlled_buffer_3_out = demultiplexer_3_out6 ? nor_1_out : 8'bz;  // Controlled_Buffer controlled_buffer_12
  assign controlled_buffer_3_out = demultiplexer_3_out1 ? register_3_q : 8'bz;  // Controlled_Buffer controlled_buffer_13
  assign controlled_buffer_3_out = demultiplexer_3_out2 ? register_4_q : 8'bz;  // Controlled_Buffer controlled_buffer_14
  and and_6 (and_6_out, demultiplexer_3_out7, ~and_2_out);  // AND_Gate
  Bit_Extender #(.out_width(7)) bit_extender_1 (.in(controlled_buffer_3_out), .out(bit_extender_1_out));
  assign controlled_buffer_3_out = and_6_out ? ram_1_dout : 8'bz;  // Controlled_Buffer controlled_buffer_15
  TTY #(.cols(40)) tty_1 (.data(bit_extender_1_out), .clk(clock_1_out), .we(demultiplexer_4_out15), .clr(button_1_out));
  Button button_1 (.out(button_1_out));
  D_Flip_Flop d_ff_1 (
    .D(adder_1_cout), .clk(demultiplexer_3_out3), .Q(d_ff_1_q), .reset(button_2_out));  // open: Qn, preset
  or or_10 (or_10_out, demultiplexer_2_out12, demultiplexer_2_out13, or_3_out);
  and and_7 (and_7_out, clock_1_out, or_10_out);
  and and_8 (and_8_out, or_10_out, nor_2_out);
  nor nor_2 (nor_2_out, controlled_buffer_3_out[0], controlled_buffer_3_out[1], controlled_buffer_3_out[2], controlled_buffer_3_out[3], controlled_buffer_3_out[4], controlled_buffer_3_out[5], controlled_buffer_3_out[6], controlled_buffer_3_out[7]);
  Button button_2 (.out(button_2_out));
  assign controlled_buffer_3_out = demultiplexer_5_out1 ? d_ff_3_q : 8'bz;  // Controlled_Buffer controlled_buffer_16
  D_Flip_Flop d_ff_2 (.D(or_11_out), .clk(or_12_out), .Q(d_ff_2_q), .reset(button_2_out));  // open: Qn, preset
  or or_11 (or_11_out, and_8_out, and_10_out);
  or or_12 (or_12_out, and_7_out, and_9_out);
  and and_9 (and_9_out, or_4_out, clock_1_out);
  nor nor_3 (nor_3_out, counter_2_q[0], counter_2_q[1], counter_2_q[2], counter_2_q[3], counter_2_q[4], counter_2_q[5], counter_2_q[6], counter_2_q[7]);
  Register register_5 (
    .D(controlled_buffer_3_out), .en(demultiplexer_4_out0), .clk(clock_1_out),
    .Q({register_5_q[6], d_ff_3_q[7:1]}));  // open: clr
  assign controlled_buffer_3_out = demultiplexer_5_out0 ? {d_ff_3_q[0], register_5_q[6], d_ff_3_q[7:2]} : 8'bz;  // Controlled_Buffer controlled_buffer_17
  xor xor_1 (xor_1_out, register_1_q[0], d_ff_1_q);
  and and_10 (and_10_out, nor_3_out, or_4_out);
  and and_11 (and_11_out, register_1_q[2], xor_1_out);
  or or_13 (or_13_out, and_16_out, and_11_out, and_15_out);
  xor xor_2 (xor_2_out, register_1_q[1], d_ff_2_q);
  // RGB_Video #(.height(256), .width(256)) rgb_video_1: pin names not known; wires that end beside it: button_1_out, clock_1_out, demultiplexer_4_out14, rgb_video_1_p4, rgb_video_1_p5, controlled_buffer_3_out
  and and_12 (and_12_out, clock_1_out, or_14_out);
  or or_14 (or_14_out, demultiplexer_5_out0, demultiplexer_5_out1);
  and and_13 (and_13_out, d_ff_3_q[1], demultiplexer_5_out0);
  or or_15 (or_15_out, and_13_out, and_14_out);
  and and_14 (and_14_out, demultiplexer_5_out1, register_5_q[6]);
  D_Flip_Flop d_ff_3 (
    .D(or_13_out), .clk(demultiplexer_2_out7), .Q(d_ff_3_q[0]), .reset(button_2_out));  // open: Qn, preset
  and and_15 (and_15_out, register_1_q[3], xor_2_out);
  Register register_6 (
    .D(controlled_buffer_3_out), .en(demultiplexer_4_out13), .clk(clock_1_out), .Q(rgb_video_1_p4));  // open: clr
  Register register_7 (
    .D(controlled_buffer_3_out), .en(demultiplexer_4_out12), .clk(clock_1_out), .Q(rgb_video_1_p5));  // open: clr
  D_Flip_Flop d_ff_4 (.D(or_15_out), .clk(and_12_out), .Q(d_ff_4_q), .reset(button_2_out));  // open: Qn, preset
  xor xor_3 (xor_3_out, register_1_q[4], d_ff_4_q);
  and and_16 (and_16_out, register_1_q[5], xor_3_out);

  // Notes on the sheet:
  //   contents of rom_1 (hex, n*v repeats v):
  //   0 2 a 83 0 a 10 83 0 a 12 83 0 a 34 83 0 a 56 83 0 a 78 83 0 a 0 83 0 a 0 83 0 a 0 83 0 a 0 83 15 4
  //   14 4 0 70 a 7 1c 5 1 70 a 7 1c 5 14 4 0 70 f0 13 0 7 f0 70 0 13 20 7 1 70 f0 13 f0 70 1 13 20 7 3d 5
  //   0 7 5 70 f0 13 f1 70 5 13 20 7 4 70 f0 13 f1 70 4 13 3 70 f0 13 20 7 f1 70 3 13 2 70 f0 13 20 7 f1
  //   70 2 13 15 4 0 36 5 70 9 71 0 b0 9 13 4 70 8 71 0 b0 8 13 3 70 7 71 0 b0 7 13 2 70 6 71 0 b0 6 13 28
  //   4
endmodule
